# Fritzing sketch PasswordWalletDevBoard (saved by Fritzing 0.9.3b)
circuit board: 6.2cm x 3.9cm
breadboards: 1

parts:
  USB = female pin header, 4 pins [form="♀ (female)"]
  RFID = mystery part, 8 pins [chip_label="RFID R/W"]
  Fram = SO08 [chip_label=MB85RS2MT package=SO]
  Oled = mystery part, 7 pins [chip_label=Oled]
  B1 = Pushbutton [package="[THT]"]
  B3 = Pushbutton [package="[THT]"]
  ISP = ISP 6 pin avr [form="♀ (female)" package=THT]
  B2 = Pushbutton [package="[THT]"]
  XTAL = Crystal [frequency="16 Mhz" package=THT]
  B4 = Pushbutton [package="[THT]"]
  C1 = Ceramic Capacitor [capacitance=22pF package="100 mil [THT, multilayer]"]
  C2 = Ceramic Capacitor [capacitance=22pF package="100 mil [THT, multilayer]"]
  R5 = Resistor [tolerance=±5% resistance=330 package=THT]
  R4 = Resistor [tolerance=±5% resistance=10k package=THT]
  C3 = Ceramic Capacitor [capacitance=100nF package="100 mil [THT, multilayer]"]
  C4 = Ceramic Capacitor [capacitance=100nF package="100 mil [THT, multilayer]"]
  C5 = Ceramic Capacitor [capacitance=100nF package="100 mil [THT, multilayer]"]
  C6 = Ceramic Capacitor [capacitance=100nF package="100 mil [THT, multilayer]"]
  R1 = Resistor [tolerance=±5% resistance=22 package=THT]
  R2 = Resistor [tolerance=±5% resistance=22 package=THT]
  R3 = Resistor [tolerance=±5% resistance=10k package=THT]
  LD1086 = Voltage Regulator - 3.3V [package="TO220 [THT]"]
  C8 = Electrolytic Capacitor [capacitance=10µF package="100 mil [THT, electrolytic]"]
  C9 = Electrolytic Capacitor [capacitance=10µF package="100 mil [THT, electrolytic]"]
  C7 = Electrolytic Capacitor [capacitance=1µF package="100 mil [THT, electrolytic]"]
  Atmega32u4 = ATMEGA32U4 [package=qfn]
  LED = LED - 5mm [color="Blue (525nm)" package="5 mm [THT]"]
  R6 = Resistor [tolerance=±5% resistance=180 package=THT]
  U1 = ATMEGA32U4 [package=tqfn]  # not connected

nets:
  5V: USB.pin1, ISP.VTG, LD1086.input_voltage, C8.+, Atmega32u4.UVCC, Atmega32u4.VBUS
  N1: USB.pin2, R1.Pin_0
  N2: USB.pin3, R2.Pin_0
  GND: USB.pin4, RFID.pin6, Fram.4, Oled.pin7, B1.Pin_1, B1.Pin_2, B3.Pin_1, B3.Pin_2, ISP.GND, B2.Pin_1, B2.Pin_2, B4.Pin_1, B4.Pin_2, C1.0, C2.0, C3.0, C4.0, C5.0, C6.0, LD1086.GND, C8.-, C9.-, C7.-, Atmega32u4.UGND, Atmega32u4.GND, LED.cathode
  N3: RFID.pin1, Atmega32u4.PE6
  SCK: RFID.pin2, Fram.6, Oled.pin5, ISP.SCK, Atmega32u4.PB1(SCK)
  MOSI: RFID.pin3, Fram.5, Oled.pin4, ISP.MOSI, Atmega32u4.PB2(MOSI)
  MISO: RFID.pin4, Fram.2, R5.Pin_1
  N4: RFID.pin7, Atmega32u4.PB0(SS)
  3.3V: RFID.pin8, Fram.8, Oled.pin6, R4.Pin_1, R3.Pin_1, LD1086.Output_Voltage, C9.+, Atmega32u4.VCC, Atmega32u4.AVCC, Atmega32u4.AREF
  N5: Fram.1, Atmega32u4.PC7
  N6: Fram.3, Fram.7, R4.Pin_0
  N7: Oled.pin1, Atmega32u4.PF6(ADC6)
  N8: Oled.pin2, Atmega32u4.PF4(ADC4)
  N9: Oled.pin3, Atmega32u4.PF0(ADC0)
  N10: B1.Pin_3, B1.Pin_4, C3.1, Atmega32u4.PC6
  N11: B3.Pin_3, B3.Pin_4, C5.1, Atmega32u4.PD4(ADC8)
  N12: ISP.MISO, R5.Pin_0, Atmega32u4.PB3(MISO)
  RST: ISP.RST, R3.Pin_0, Atmega32u4.!RESET
  N13: B2.Pin_3, B2.Pin_4, C4.1, Atmega32u4.PB4(ADC11)
  N14: XTAL.pin_0, C1.1, Atmega32u4.XTAL1
  N15: XTAL.pin_1, C2.1, Atmega32u4.XTAL2
  N16: B4.Pin_3, B4.Pin_4, C6.1, Atmega32u4.PB6(ADC13)
  N17: R1.Pin_1, Atmega32u4.D+
  N18: R2.Pin_1, Atmega32u4.D-
  N19: C7.+, Atmega32u4.UCAP
  N20: Atmega32u4.PD5, R6.Pin_1
  N21: LED.anode, R6.Pin_0

notes:
  VBUS
  D+
  D-
  GND
  OUT
  IN
  Dev board v1
  Thomas Chevalier
  2017

custom parts:
  ISP 6 pin avr: ISP 6 pin for avr
  Voltage Regulator - 3.3V: 3.3V DC Voltage Regulator
