# Fritzing sketch isp (saved by Fritzing 0.9.2b)
breadboards: 1

parts:
  U2 = ATMEGA32U4 [package=qfn]
  C4 = Electrolytic Capacitor [capacitance=1µF package="100 mil [THT, electrolytic]"]
  R3 = Resistor [tolerance=±5% resistance=330 package=THT]
  S2 = Pushbutton [package="[THT]"]
  R4 = Resistor [tolerance=±5% resistance=10k package=THT]
  XTAL2 = Crystal [frequency="16 Mhz" package=THT]
  C5 = Ceramic Capacitor [capacitance=22pF package="100 mil [THT, multilayer]"]
  C6 = Ceramic Capacitor [capacitance=22pF package="100 mil [THT, multilayer]"]
  Composant1 = Arduino Uno (Rev3)

nets:
  N1: U2.UVCC, U2.VBUS, U2.VCC, U2.AVCC, U2.AREF, R4.Pin_0
  N2: U2.UGND, U2.GND, C4.-, S2.Pin_1, S2.Pin_2, C5.0, C6.1
  N3: U2.UCAP, C4.+
  N4: U2.!RESET, R3.Pin_0, R4.Pin_1, Composant1.D10_PWM/SS
  N5: U2.XTAL2, XTAL2.pin_0, C5.1
  N6: U2.XTAL1, XTAL2.pin_1, C6.0
  N7: R3.Pin_1, S2.Pin_3, S2.Pin_4
