# Fritzing sketch Atmega32u4 (saved by Fritzing 0.9.3b)
circuit board: 5.52336cm x 4cm
breadboards: 1

parts:
  Atmega32u4 = ATMEGA32U4 [package=qfn]
  USB = female pin header, 4 pins [form="♀ (female)"]
  RFID2 = mystery part, 8 pins [chip_label="RFID R/W"]
  Fram = SO08 [chip_label=MB85RS2MT package=SO]
  Oled = mystery part, 7 pins [chip_label=Oled]
  B1 = Pushbutton [package="[THT]"]
  B3 = Pushbutton [package="[THT]"]
  ISP = ISP 6 pin avr [form="♀ (female)" package=THT]
  R1 = Resistor [tolerance=±5% resistance=330 package="0603 [SMD]"]
  R3 = Resistor [tolerance=±5% resistance=22 package="0603 [SMD]"]
  R2 = Resistor [tolerance=±5% resistance=22 package="0603 [SMD]"]
  R5 = Resistor [tolerance=±5% resistance=10k package="0603 [SMD]"]
  R4 = Resistor [tolerance=±5% resistance=10k package="0603 [SMD]"]
  R7 = Resistor [tolerance=±5% resistance=330 package="0603 [SMD]"]
  R8 = Resistor [tolerance=±5% resistance=330 package="0603 [SMD]"]
  C3 = Ceramic Capacitor [capacitance=100nF package="0603 [SMD, multilayer]"]
  C1 = Ceramic Capacitor [capacitance=22pF package="0603 [SMD, multilayer]"]
  B2 = Pushbutton [package="[THT]"]
  C4 = Ceramic Capacitor [capacitance=1µF package="0603 [SMD, multilayer]"]
  BRES = Pushbutton [package="[SMD]"]
  LD1086 = Voltage Regulator - 5V [package="DPak [SMD]"]
  C5 = Ceramic Capacitor [capacitance=10µF package="0603 [SMD, multilayer]"]
  C6 = Ceramic Capacitor [capacitance=10µF package="0603 [SMD, multilayer]"]
  R6 = Resistor [tolerance=±5% resistance=330 package="0603 [SMD]"]
  C10 = Ceramic Capacitor [capacitance=100nF package="0603 [SMD, multilayer]"]
  C8 = Ceramic Capacitor [capacitance=100nF package="0603 [SMD, multilayer]"]
  C9 = Ceramic Capacitor [capacitance=100nF package="0603 [SMD, multilayer]"]
  C7 = Electrolytic Capacitor [package="100 mil [THT, electrolytic]"]
  XTAL1 = Crystal [frequency="16 Mhz" package=THT]
  B4 = Pushbutton [package="[THT]"]

nets:
  5V: Atmega32u4.UVCC, Atmega32u4.VBUS, USB.pin1, ISP.VTG, LD1086.input_voltage, C5.1, C7.+
  N1: Atmega32u4.D-, R3.Pin_1
  N2: Atmega32u4.D+, R2.Pin_1
  GND: Atmega32u4.UGND, Atmega32u4.GND, Atmega32u4.PE2_!HWB, USB.pin4, RFID2.pin6, Fram.4, Oled.pin7, B1.Pin_1, B1.Pin_2, B3.Pin_1, B3.Pin_2, ISP.GND, C3.0, C1.0, B2.Pin_1, B2.Pin_2, C4.0, BRES.Pin_1, BRES.Pin_2, LD1086.GND, C5.0, C6.0, C10.0, C8.0, C9.0, C7.-, B4.Pin_1, B4.Pin_2
  N3: Atmega32u4.UCAP, C4.1
  N4: Atmega32u4.PB1(SCK), ISP.SCK, R6.Pin_0
  N5: Atmega32u4.PB2(MOSI), ISP.MOSI, R7.Pin_0
  N6: Atmega32u4.PB3(MISO), ISP.MISO, R8.Pin_0
  RST: Atmega32u4.!RESET, ISP.RST, R1.Pin_0, R4.Pin_0
  3.3V: Atmega32u4.VCC, Atmega32u4.AVCC, Atmega32u4.AREF, RFID2.pin8, Fram.8, Oled.pin6, R5.Pin_1, R4.Pin_1, LD1086.output_voltage, C6.1
  N7: Atmega32u4.XTAL2, C3.1, XTAL1.pin_1
  N8: Atmega32u4.XTAL1, C1.1, XTAL1.pin_0
  N9: Atmega32u4.PD0(SCL), Oled.pin1
  N10: Atmega32u4.PD1(SDA), Oled.pin2
  N11: Atmega32u4.PD2(RX), Oled.pin3
  N12: Atmega32u4.PD4(ADC8), B1.Pin_3, B1.Pin_4, C8.1
  N13: Atmega32u4.PD6(ADC9), RFID2.pin1
  N14: Atmega32u4.PB4(ADC11), B2.Pin_3, B2.Pin_4, C9.1
  N15: Atmega32u4.PB6(ADC13), B4.Pin_3, B4.Pin_4
  N16: Atmega32u4.PC6, RFID2.pin7
  N17: Atmega32u4.PC7, B3.Pin_3, B3.Pin_4, C10.1
  N18: Atmega32u4.PF7(ADC7), Fram.1
  N19: USB.pin2, R2.Pin_0
  N20: USB.pin3, R3.Pin_0
  SCK: RFID2.pin2, Fram.6, Oled.pin5, R6.Pin_1
  MOSI: RFID2.pin3, Fram.5, Oled.pin4, R7.Pin_1
  MISO: RFID2.pin4, Fram.2, R8.Pin_1
  N21: Fram.3, Fram.7, R5.Pin_0
  N22: R1.Pin_1, BRES.Pin_3, BRES.Pin_4

notes:
  VBUS
  D+
  D-
  GND

custom parts:
  ISP 6 pin avr: ISP 6 pin for avr
  Voltage Regulator - 5V: 5V DC Voltage Regulator
  Electrolytic Capacitor: A small electrolytic capacitor
