# Fritzing sketch PasswordWalletDevBoardTQFP2 (saved by Fritzing 0.9.3b)
circuit board: 6.2cm x 3.9cm
breadboards: 1

parts:
  RFID = mystery part, 8 pins [chip_label="RFID R/W"]
  Oled_display = mystery part, 7 pins [chip_label=Oled]
  B1 = Pushbutton [package="[THT]"]
  B3 = Pushbutton [package="[THT]"]
  ISP = ISP 6 pin avr [form="♀ (female)" package=THT]
  B2 = Pushbutton [package="[THT]"]
  XTAL = Crystal [frequency="16 Mhz" package=THT]
  B4 = Pushbutton [package="[THT]"]
  C1 = Ceramic Capacitor [capacitance=22pF package="100 mil [THT, multilayer]"]
  C2 = Ceramic Capacitor [capacitance=22pF package="100 mil [THT, multilayer]"]
  R5 = Resistor [tolerance=±5% resistance=330 package=THT]
  R4 = Resistor [tolerance=±5% resistance=10k package=THT]
  C3 = Ceramic Capacitor [capacitance=100nF package="100 mil [THT, multilayer]"]
  C4 = Ceramic Capacitor [capacitance=100nF package="100 mil [THT, multilayer]"]
  C5 = Ceramic Capacitor [capacitance=100nF package="100 mil [THT, multilayer]"]
  C6 = Ceramic Capacitor [capacitance=100nF package="100 mil [THT, multilayer]"]
  R1 = Resistor [tolerance=±5% resistance=22 package=THT]
  R2 = Resistor [tolerance=±5% resistance=22 package=THT]
  R3 = Resistor [tolerance=±5% resistance=10k package=THT]
  LD1086 = Voltage Regulator - 3.3V [package="TO220 [THT]"]
  C8 = Electrolytic Capacitor [capacitance=10µF package="100 mil [THT, electrolytic]"]
  C9 = Electrolytic Capacitor [capacitance=10µF package="100 mil [THT, electrolytic]"]
  LED = LED - 5mm [color="Blue (525nm)" package="5 mm [THT]"]
  R6 = Resistor [tolerance=±5% resistance=180 package=THT]
  C7 = Electrolytic Capacitor [capacitance=1µF package="100 mil [THT, electrolytic]"]
  USB = USB Connectors [package=usb-a-h]
  Fram = SO08 [chip_label=MB85RS2MT package=SO]
  C10 = Ceramic Capacitor [capacitance=100nF package="100 mil [THT, multilayer]"]
  Atmega32u4 = ATMEGA32U4 [package=tqfn]

nets:
  N1: RFID.pin1, Atmega32u4.PE6
  SCK: RFID.pin2, Oled_display.pin5, ISP.SCK, Fram.6, Atmega32u4.PB1(SCK)
  MOSI: RFID.pin3, Oled_display.pin4, ISP.MOSI, Fram.5, Atmega32u4.PB2(MOSI)
  MISO: RFID.pin4, R5.Pin_1, Fram.2
  GND: RFID.pin6, Oled_display.pin7, B1.Pin_1, B1.Pin_2, B3.Pin_1, B3.Pin_2, ISP.GND, B2.Pin_1, B2.Pin_2, B4.Pin_1, B4.Pin_2, C1.0, C2.0, C3.0, C4.0, C5.0, C6.0, LD1086.GND, C8.-, C9.-, LED.cathode, C7.-, USB.GND, Fram.4, C10.0, Atmega32u4.UGND, Atmega32u4.GND, Atmega32u4.PE2_!HWB
  N2: RFID.pin7, Atmega32u4.PB0(SS)
  3.3V: RFID.pin8, Oled_display.pin6, R4.Pin_1, R3.Pin_1, LD1086.Output_Voltage, C9.+, Fram.8, C10.1, Atmega32u4.VCC, Atmega32u4.AVCC, Atmega32u4.AREF
  N3: Oled_display.pin1, Atmega32u4.PF6(ADC6)
  N4: Oled_display.pin2, Atmega32u4.PF4(ADC4)
  N5: Oled_display.pin3, Atmega32u4.PF0(ADC0)
  N6: B1.Pin_3, B1.Pin_4, C3.1, Atmega32u4.PC6
  N7: B3.Pin_3, B3.Pin_4, C5.1, Atmega32u4.PD4(ADC8)
  N8: ISP.MISO, R5.Pin_0, Atmega32u4.PB3(MISO)
  RST: ISP.RST, R3.Pin_0, Atmega32u4.!RESET
  5V: ISP.VTG, LD1086.input_voltage, C8.+, USB.VBUS, Atmega32u4.UVCC, Atmega32u4.VBUS
  N9: B2.Pin_3, B2.Pin_4, C4.1, Atmega32u4.PB4(ADC11)
  N10: XTAL.pin_0, C1.1, Atmega32u4.XTAL1
  N11: XTAL.pin_1, C2.1, Atmega32u4.XTAL2
  N12: B4.Pin_3, B4.Pin_4, C6.1, Atmega32u4.PB6(ADC13)
  N13: R4.Pin_0, Fram.3, Fram.7
  N14: R1.Pin_0, USB.D+
  N15: R1.Pin_1, Atmega32u4.D+
  N16: R2.Pin_0, USB.D-
  N17: R2.Pin_1, Atmega32u4.D-
  N18: LED.anode, R6.Pin_0
  N19: R6.Pin_1, Atmega32u4.PD5
  N20: C7.+, Atmega32u4.UCAP
  N21: Fram.1, Atmega32u4.PC7

notes:
  VBUS
  D+
  D-
  GND
  OUT
  IN
  Dev board v1
  Thomas Chevalier
  2017
  5V
  RFID
  3V3
  v1 - 2017

custom parts:
  ISP 6 pin avr: ISP 6 pin for avr
  Voltage Regulator - 3.3V: 3.3V DC Voltage Regulator
  USB Connectors: USB Connectors USB-B-PTH is fully proven SKU : PRT-00139 USB-miniB is fully proven SKU : PRT-00587 USB-A-PCB is untested. USB-A-H is throughly reviewed, but untested. Spark Fun Electronics SKU : PRT-00437 USB-B-SMT is throughly reviewed, but untested. Needs silkscreen touching up. USB-A-S has not been used/tested USB-MB-H has not been used/tested
