# Fritzing sketch minimal (saved by Fritzing 0.9.2b)
breadboards: 1

parts:
  U1 = ATMEGA32U4 [package=qfn]
  C1 = Electrolytic Capacitor [capacitance=1µF package="100 mil [THT, electrolytic]"]
  R1 = Resistor [tolerance=±5% resistance=10k package=THT]
  R2 = Resistor [tolerance=±5% resistance=330 package=THT]
  S1 = Pushbutton [package="[THT]"]
  XTAL1 = Crystal [frequency="16 Mhz" package=THT]
  C2 = Ceramic Capacitor [capacitance=22pF package="100 mil [THT, multilayer]"]
  C3 = Ceramic Capacitor [capacitance=22pF package="100 mil [THT, multilayer]"]

nets:
  N1: U1.UVCC, U1.VBUS, U1.VCC, U1.AVCC, U1.AREF, R1.Pin_0
  N2: U1.UGND, U1.GND, C1.-, S1.Pin_1, S1.Pin_2, C2.0, C3.1
  N3: U1.UCAP, C1.+
  N4: U1.!RESET, R1.Pin_1, R2.Pin_0
  N5: U1.XTAL2, XTAL1.pin_0, C2.1
  N6: U1.XTAL1, XTAL1.pin_1, C3.0
  N7: R2.Pin_1, S1.Pin_3, S1.Pin_4
